# Fritzing sketch BetterParkingAidTransmitter (saved by Fritzing 0.9.3b)
stripboards: 1

parts:
  C5 = Ceramic Capacitor [capacitance=100nF package="100 mil [THT, multilayer]"]
  P2 = S1133 Si Photodiode [package="8mm Ceramic [THT]"]
  C6 = Ceramic Capacitor [capacitance=100nF package="100 mil [THT, multilayer]"]
  R9 = Resistor [tolerance=±5% resistance=1k package="1206 [SMD]"]
  R10 = Resistor [tolerance=±5% resistance=1k package="1206 [SMD]"]
  R11 = Resistor [tolerance=±5% resistance=1k package="1206 [SMD]"]
  D4 = Diode [package=diode-1n4148]  # not connected
  D5 = Diode [package=diode-1n4148]
  LED5 = smd LED [color="Red (633nm)" package="1206 [SMD]"]
  LED6 = smd LED [color="Orange (612nm)" package="1206 [SMD]"]
  LED7 = smd LED [color="Green (555nm)" package="1206 [SMD]"]
  U4 = 555 Timer [package="DIP8 [THT]"]
  U5 = LM124-324 Quad Opamp [package="DIP (Dual Inline)"]
  R12 = Resistor [tolerance=±5% resistance=10k package=THT]
  C7 = Ceramic Capacitor [capacitance=10nF package="100 mil [THT, multilayer]"]
  LED8 = LED - 5mm [color="Infrared (940nm)" package="5 mm [THT]"]
  C8 = Electrolytic Capacitor [capacitance=1µF package="100 mil [THT, electrolytic]"]
  VCC2 = Battery block 9V
  R13 = Resistor [tolerance=±5% resistance=1M package="0603 [SMD]"]
  R14 = Resistor [tolerance=±5% resistance=1k package=THT]
  R15 = Resistor [tolerance=±5% resistance=33 package=THT]
  C9 = Electrolytic Capacitor [capacitance=1µF package="100 mil [THT, electrolytic]"]
  R16 = Resistor [tolerance=±5% resistance=1M package="1206 [SMD]"]
  R17 = Resistor [tolerance=±5% resistance=1k package="1206 [SMD]"]
  R18 = Resistor [tolerance=±5% resistance=1.5k package="1206 [SMD]"]
  R19 = Resistor [tolerance=±5% resistance=4.7k package="1206 [SMD]"]
  R20 = Resistor [tolerance=±5% resistance=1k package="1206 [SMD]"]
  R21 = Resistor [tolerance=±5% resistance=1k package="1206 [SMD]"]
  R22 = Resistor [tolerance=±5% resistance=1k package="1206 [SMD]"]

nets:
  N1: C5.0, C5.1, P2.cathode, P2.anode, C6.0, C6.1, R9.Pin_0, R9.Pin_1, R10.Pin_0, R10.Pin_1, R11.Pin_0, R11.Pin_1, D5.A, D5.C, LED5.cathode, LED5.anode, LED6.cathode, LED6.anode, LED7.anode, U4.Ground, U4.Output, U4.Reset, U4.Control_Voltage, U4.Threshold, U4.Vcc_Supply_Voltage, U5.1OUT, U5.1IN-, U5.1IN+, U5.VCC+, U5.2IN+, U5.2IN-, U5.2OUT, U5.3OUT, U5.3IN-, U5.3IN+, U5.VCC-, U5.4IN+, U5.4IN-, U5.4OUT, R12.Pin_0, R12.Pin_1, C7.0, C7.1, LED8.cathode, C8.-, C8.+, VCC2.-, VCC2.+, R13.Pin_0, R13.Pin_1, R14.Pin_1, R15.Pin_0, C9.-, C9.+, R16.Pin_0, R16.Pin_1, R17.Pin_0, R17.Pin_1, R18.Pin_0, R18.Pin_1, R19.Pin_0, R19.Pin_1, R20.Pin_0, R20.Pin_1, R21.Pin_0, R21.Pin_1, R22.Pin_0
  N2: LED7.cathode, R22.Pin_1
  N3: U4.Trigger, U4.Discharge, R14.Pin_0
  N4: LED8.anode, R15.Pin_1
