# Fritzing sketch ParkingAid_Reciever (saved by Fritzing 0.9.3b)
stripboards: 1

parts:
  U1 = LM124-324 Quad Opamp [package="DIP (Dual Inline)"]
  P1 = S1133 Si Photodiode [package="8mm Ceramic [THT]"]
  C1 = Capacitor [package=cap-pth-5mm]
  R1 = Resistor [tolerance=±5% resistance=1k package="0603 [SMD]"]
  C2 = Capacitor [package=cap-pth-5mm]
  R2 = Resistor [tolerance=±5% resistance=220 package="0603 [SMD]"]
  D1 = Diode [package=diode-hv]
  D2 = Diode [package=diode-hv]  # not connected
  R3 = Resistor [tolerance=±5% resistance=220 package="0603 [SMD]"]
  R4 = Resistor [tolerance=±5% resistance=1M package="0603 [SMD]"]
  VCC1 = Battery block 9V

nets:
  N1: U1.1OUT, U1.4OUT, C1.2, C2.1, R3.Pin_0
  N2: U1.1IN-, U1.2OUT, U1.3OUT, U1.4IN-, P1.anode, C1.1, R1.Pin_1, R2.Pin_0, R2.Pin_1, R3.Pin_1, R4.Pin_1
  N3: U1.1IN+, U1.2IN+, U1.3IN+, U1.4IN+, P1.cathode, D1.A, VCC1.-
  N4: U1.VCC+, U1.VCC-, VCC1.+
  N5: U1.2IN-, U1.3IN-
  N6: R1.Pin_0, C2.2, R4.Pin_0
