# Fritzing sketch ParkingAid_transhmitter (saved by Fritzing 0.9.3b)
circuit board: 8.46667cm x 5.64444cm
stripboards: 1

parts:
  R2 = Resistor [tolerance=±5% resistance=10k package=THT]
  C1 = Electrolytic Capacitor [capacitance=1µF package="100 mil [THT, electrolytic]"]
  C2 = Ceramic Capacitor [capacitance=10nF package="100 mil [THT, multilayer]"]
  LED1 = LED - 5mm [color="Infrared (940nm)" package="5 mm [THT]"]
  VCC1 = Battery block 9V
  R3 = Resistor [tolerance=±5% resistance=1k package=THT]
  R1 = Resistor [tolerance=±5% resistance=33 package=THT]
  U2 = 555 Timer [package="DIP8 [THT]"]
  U3 = LM124-324 Quad Opamp [package="DIP (Dual Inline)"]
  R5 = Resistor [tolerance=±5% resistance=1M package="0603 [SMD]"]
  C3 = Ceramic Capacitor [capacitance=100nF package="100 mil [THT, multilayer]"]
  P1 = S1133 Si Photodiode [package="8mm Ceramic [THT]"]
  C4 = Ceramic Capacitor [capacitance=100nF package="100 mil [THT, multilayer]"]
  R6 = Resistor [tolerance=±5% resistance=1k package="1206 [SMD]"]  # not connected
  D2 = Diode [package=diode-1n4148]  # not connected
  R7 = Resistor [tolerance=±5% resistance=1k package="1206 [SMD]"]  # not connected
  D3 = Diode [package=diode-1n4148]  # not connected
  C5 = Electrolytic Capacitor [capacitance=1µF package="100 mil [THT, electrolytic]"]  # not connected
  R8 = Resistor [tolerance=±5% resistance=1M package=THT]  # not connected
  R9 = Resistor [tolerance=±5% resistance=1k package="1206 [SMD]"]
  R10 = Resistor [tolerance=±5% resistance=1k package="1206 [SMD]"]
  R11 = Resistor [tolerance=±5% resistance=1k package="1206 [SMD]"]
  LED3 = smd LED [color="Red (633nm)" package="1206 [SMD]"]
  LED4 = smd LED [color="Red (633nm)" package="1206 [SMD]"]
  LED2 = smd LED [color="Red (633nm)" package="1206 [SMD]"]
  R12 = Resistor [tolerance=±5% resistance=4.7k package="1206 [SMD]"]

nets:
  N1: R2.Pin_0, R2.Pin_1, C1.-, C1.+, C2.0, C2.1, LED1.cathode, LED1.anode, VCC1.-, VCC1.+, R3.Pin_1, R1.Pin_0, R1.Pin_1, U2.Ground, U2.Output, U2.Reset, U2.Control_Voltage, U2.Threshold, U2.Vcc_Supply_Voltage, U3.1OUT, U3.1IN-, U3.1IN+, U3.VCC+, U3.2OUT, U3.3OUT, U3.VCC-, U3.4IN+, U3.4IN-, U3.4OUT, R5.Pin_0, R5.Pin_1, C3.0, C3.1, P1.cathode, P1.anode, C4.0, C4.1, R9.Pin_0, R9.Pin_1, R10.Pin_0, R11.Pin_0, R11.Pin_1, LED3.cathode, LED3.anode, LED4.cathode, LED4.anode, LED2.cathode, LED2.anode, R12.Pin_0, R12.Pin_1
  N2: R3.Pin_0, U2.Trigger, U2.Discharge
  N3: U3.2IN+, U3.3IN+
  N4: U3.2IN-, U3.3IN-, R10.Pin_1
